// Digital circuit PassCircuit.dig as structural Verilog
module PassCircuit (
  input  A,
  input  B,
  input  C,
  input  clk,
  output [7:0] Z
);

  wire and_1_out, and_2_out, and_3_out, and_4_out, and_5_out, and_6_out, and_7_out, and_8_out, and_9_out,
       and_10_out, and_11_out, and_12_out, and_13_out, and_14_out, and_15_out, not_1_out, not_2_out,
       not_3_out;

  not not_1 (not_1_out, A);
  not not_2 (not_2_out, B);
  not not_3 (not_3_out, C);
  and and_1 (and_1_out, not_1_out, not_2_out, C);
  and and_2 (and_2_out, A, not_3_out);
  and and_3 (and_3_out, A, B);
  and and_4 (and_4_out, B, not_3_out);
  and and_5 (and_5_out, not_1_out, C);
  and and_6 (and_6_out, A, not_2_out);
  and and_7 (and_7_out, not_1_out, B);
  and and_8 (and_8_out, A, not_2_out);
  and and_9 (and_9_out, not_2_out, not_3_out);
  and and_10 (and_10_out, not_1_out, B, not_3_out);
  and and_11 (and_11_out, A, not_2_out, not_3_out);
  and and_12 (and_12_out, A, B, C);
  and and_13 (and_13_out, not_1_out, not_2_out, C);
  and and_14 (and_14_out, A, not_3_out);
  and and_15 (and_15_out, B, not_3_out);
  or or_1 (Z[3], and_5_out, and_6_out);
  or or_2 (Z[2], and_7_out, and_8_out, and_9_out);
  or or_3 (Z[1], and_10_out, and_11_out, and_12_out);
  or or_4 (Z[0], and_13_out, and_14_out, and_15_out);
  or or_5 (Z[5], and_1_out, and_2_out, and_3_out, and_4_out);
  Terminal terminal_1 (.D({2'b01, Z[5], 1'b0, Z[3:0]}), .C(clk), .en(1'b1));

  assign {Z[7:6], Z[4]} = 3'b010;
endmodule
