// Digital circuit circuit.dig as structural Verilog
module circuit (
  input  [2:0] In,
  input  clk,
  input  in_4,
  input  in_5,
  input  in_6,
  output [7:0] Z
);

  wire and_1_out, and_2_out, and_3_out, and_4_out, and_5_out, and_6_out, and_7_out, and_8_out, and_9_out,
       and_10_out, and_11_out, and_12_out, and_13_out, and_14_out, and_15_out, not_1_out, not_2_out,
       not_3_out;

  not not_1 (not_1_out, In[0]);
  not not_2 (not_2_out, In[1]);
  not not_3 (not_3_out, In[2]);
  and and_1 (and_1_out, not_1_out, not_2_out, In[2]);
  and and_2 (and_2_out, In[0], not_3_out);
  and and_3 (and_3_out, In[0], In[1]);
  and and_4 (and_4_out, In[1], not_3_out);
  and and_5 (and_5_out, not_1_out, In[2]);
  and and_6 (and_6_out, In[0], not_2_out);
  and and_7 (and_7_out, not_1_out, In[1]);
  and and_8 (and_8_out, In[0], not_2_out);
  and and_9 (and_9_out, not_2_out, not_3_out);
  and and_10 (and_10_out, not_1_out, In[1], not_3_out);
  and and_11 (and_11_out, In[0], not_2_out, not_3_out);
  and and_12 (and_12_out, In[0], In[1], In[2]);
  and and_13 (and_13_out, not_1_out, not_2_out, In[2]);
  and and_14 (and_14_out, In[0], not_3_out);
  and and_15 (and_15_out, In[1], not_3_out);
  or or_1 (Z[3], and_5_out, and_6_out);
  or or_2 (Z[2], and_7_out, and_8_out, and_9_out);
  or or_3 (Z[1], and_10_out, and_11_out, and_12_out);
  or or_4 (Z[0], and_13_out, and_14_out, and_15_out);
  Terminal terminal_1 (.D({in_4, in_5, Z[5], in_6, Z[3:0]}), .C(clk), .en(1'b1));
  or or_5 (Z[5], and_1_out, and_2_out, and_3_out, and_4_out);

  assign {Z[7:6], Z[4]} = {in_4, in_5, in_6};

  // Other names for the same wires on the sheet: _0 = in_4; _1 = in_5; _2 = Z[5]; _3 = in_6; _4 = Z[3]; _5 = Z[2];
  //   _6 = Z[1]; _7 = Z[0]
endmodule
