// Digital circuit Excess-3.dig as structural Verilog
module Excess_3 (
  input  [3:0] Input,
  output [3:0] Out
);

  wire and_1_out, and_2_out, and_3_out, and_4_out, and_5_out, and_6_out, and_7_out, not_1_out, not_2_out;

  not not_1 (not_1_out, Input[2]);
  not not_2 (not_2_out, Input[1]);
  not not_3 (Out[0], Input[0]);
  and and_1 (and_1_out, Input[2], Input[0]);
  and and_2 (and_2_out, Input[2], Input[1]);
  and and_3 (and_3_out, not_1_out, Input[0]);
  and and_4 (and_4_out, not_1_out, Input[1]);
  and and_5 (and_5_out, Input[2], not_2_out, Out[0]);
  and and_6 (and_6_out, not_2_out, Out[0]);
  and and_7 (and_7_out, Input[1], Input[0]);
  or or_1 (Out[3], Input[3], and_1_out, and_2_out);
  or or_2 (Out[2], and_3_out, and_4_out, and_5_out);
  or or_3 (Out[1], and_6_out, and_7_out);
endmodule
