// Digital circuit cyclic.dig as structural Verilog
module cyclic (
  input  [3:0] IN,
  output [3:0] OUT
);

  wire and_2_out, and_3_out, and_4_out, and_5_out, and_6_out, and_7_out, and_8_out, not_1_out, not_2_out,
       not_3_out, not_4_out;

  not not_1 (not_1_out, IN[3]);
  not not_2 (not_2_out, IN[2]);
  not not_3 (not_3_out, IN[1]);
  not not_4 (not_4_out, IN[0]);
  and and_1 (OUT[3], IN[3], not_2_out, not_3_out);
  and and_2 (and_2_out, not_1_out, IN[2]);
  and and_3 (and_3_out, IN[3], not_2_out, not_3_out);
  and and_4 (and_4_out, not_1_out, not_2_out, IN[1]);
  and and_5 (and_5_out, not_1_out, IN[2], not_3_out);
  and and_6 (and_6_out, not_1_out, IN[1], not_4_out);
  and and_7 (and_7_out, not_1_out, not_3_out, IN[0]);
  and and_8 (and_8_out, not_2_out, not_3_out, IN[0]);
  or or_1 (OUT[2], and_2_out, and_3_out);
  or or_2 (OUT[1], and_4_out, and_5_out);
  or or_3 (OUT[0], and_6_out, and_7_out, and_8_out);
endmodule
