// Digital circuit Templatet.dig as structural Verilog
module Templatet (
  input  [3:0] In,
  input  [1:0] Selector,
  output [3:0] Output
);

  wire [3:0] code642_3_1_out, code2421_1_out, cyclic_1_out, excess_3_1_out;

  Excess_3 excess_3_1 (.Input(In), .Out(excess_3_1_out));
  cyclic cyclic_1 (.IN(In), .OUT(cyclic_1_out));
  code2421 code2421_1 (.IN(In), .OUT(code2421_1_out));
  code642_3 code642_3_1 (.IN(In), .OUT(code642_3_1_out));
  Multiplexer #(.Bits(4), .Selector_Bits(2)) multiplexer_1 (
    .sel(Selector), .in_0(excess_3_1_out), .in_1(cyclic_1_out), .in_2(code2421_1_out),
    .in_3(code642_3_1_out), .out(Output));
endmodule
