// Digital circuit CCircuit.dig as structural Verilog
module CCircuit (
  input  [6:0] BitToInvert,
  input  m4,
  input  m3,
  input  m2,
  input  p3,
  input  m1,
  input  p2,
  input  p1,
  output [6:0] OUTPUTto
);

  xor xor_1 (OUTPUTto[0], m4, BitToInvert[0]);
  xor xor_2 (OUTPUTto[1], m3, BitToInvert[1]);
  xor xor_3 (OUTPUTto[2], m2, BitToInvert[2]);
  xor xor_4 (OUTPUTto[3], p3, BitToInvert[3]);
  xor xor_5 (OUTPUTto[4], m1, BitToInvert[4]);
  xor xor_6 (OUTPUTto[5], p2, BitToInvert[5]);
  xor xor_7 (OUTPUTto[6], p1, BitToInvert[6]);
endmodule
