// Digital circuit bitInvertor.dig as structural Verilog
module bitInvertor (
  input  A,
  input  B,
  input  C,
  output [6:0] CONVERT_SIG
);

  wire not_1_out, not_2_out, not_3_out;

  not not_1 (not_1_out, A);
  not not_2 (not_2_out, B);
  not not_3 (not_3_out, C);
  and and_1 (CONVERT_SIG[6], not_1_out, not_2_out, C);
  and and_2 (CONVERT_SIG[5], not_1_out, B, not_3_out);
  and and_3 (CONVERT_SIG[4], not_1_out, B, C);
  and and_4 (CONVERT_SIG[3], A, not_2_out, not_3_out);
  and and_5 (CONVERT_SIG[2], A, not_2_out, C);
  and and_6 (CONVERT_SIG[1], A, B, not_3_out);
  and and_7 (CONVERT_SIG[0], A, B, C);
endmodule
