// Digital circuit 2ndCom.dig as structural Verilog
module _2ndCom (
  input  _0,
  input  _1,
  input  _2,
  input  _3,
  input  _4,
  input  _5,
  input  _6,
  input  _7,
  output O0,
  output O1,
  output O2,
  output O3,
  output O4,
  output O5,
  output O6,
  output O7,
  output O8
);

  wire half_1_c, half_2_c, half_3_c, half_4_c, half_5_c, half_6_c, half_7_c, half_8_c, half_9_c;

  Half half_1 (.A(_7), .B(half_3_c), .S(O7), .C(half_1_c));
  Half half_2 (.A(half_1_c), .B(half_2_c), .S(O8), .C(half_2_c));
  Half half_3 (.A(_6), .B(half_4_c), .S(O6), .C(half_3_c));
  Half half_4 (.A(_5), .B(half_5_c), .S(O5), .C(half_4_c));
  Half half_5 (.A(_4), .B(half_6_c), .S(O4), .C(half_5_c));
  Half half_6 (.A(_3), .B(half_7_c), .S(O3), .C(half_6_c));
  Half half_7 (.A(_2), .B(half_8_c), .S(O2), .C(half_7_c));
  Half half_8 (.A(_1), .B(half_9_c), .S(O1), .C(half_8_c));
  Half half_9 (.A(_0), .B(1'b1), .S(O0), .C(half_9_c));
  // also tied to GND on the sheet: half_2_c
endmodule
