// Digital circuit Full.dig as structural Verilog
module Full (
  input  A,
  input  B,
  input  CI,
  output S,
  output Co
);

  wire and_1_out, and_2_out, xor_1_out;

  xor xor_1 (xor_1_out, A, B);
  xor xor_2 (S, xor_1_out, CI);
  and and_1 (and_1_out, xor_1_out, CI);
  and and_2 (and_2_out, A, B);
  or or_1 (Co, and_1_out, and_2_out);
endmodule
