// Digital circuit Template.dig as structural Verilog
module Template (
  input  [7:0] In,
  output [8:0] Output
);

  wire _2ndcom_1_o8, not_1_out, not_2_out, not_3_out, not_4_out, not_5_out, not_6_out, not_8_out, not_9_out;

  not not_1 (not_1_out, In[7]);
  not not_2 (not_2_out, In[6]);
  not not_3 (not_3_out, In[5]);
  not not_4 (not_4_out, In[4]);
  not not_5 (not_5_out, In[3]);
  not not_6 (not_6_out, In[2]);
  not not_7 (not_6_out, In[2]);
  not not_8 (not_8_out, In[1]);
  not not_9 (not_9_out, In[0]);
  _2ndCom _2ndcom_1 (
    ._0(not_9_out), ._1(not_8_out), ._2(not_6_out), ._3(not_5_out), ._4(not_4_out), ._5(not_3_out),
    ._6(not_2_out), ._7(not_1_out), .O0(Output[0]), .O1(Output[1]), .O2(Output[2]), .O3(Output[3]),
    .O4(Output[4]), .O5(Output[5]), .O6(Output[6]), .O7(Output[7]), .O8(_2ndcom_1_o8));
  // And and_1 is placed but not wired
  not not_10 (Output[8], _2ndcom_1_o8);
endmodule
