// Digital circuit 2ndComplement.dig as structural Verilog
module _2ndComplement (
  input  _0,
  input  _1,
  input  _2,
  output O0,
  output O1,
  output O2,
  output O3
);

  wire half_1_c, half_3_c, not_1_out, not_2_out, not_3_out;

  or or_1 (O3, O2, O1, O0);
  not not_1 (not_1_out, _2);
  not not_2 (not_2_out, _1);
  Half half_1 (.A(not_2_out), .B(half_3_c), .S(O1), .C(half_1_c));
  Half half_2 (.A(not_1_out), .B(half_1_c), .S(O2));  // open: C
  not not_3 (not_3_out, _0);
  Half half_3 (.A(not_3_out), .B(1'b1), .S(O0), .C(half_3_c));
endmodule
