// Digital circuit Lab4.dig as structural Verilog
module Lab4 (
  input  [3:0] In,
  output [3:0] Output
);

  wire [3:0] undriven;

  // _2ndComplement _2ndcomplement_1: pin names not known; wires that end beside it: In[0], In[1], In[2]
  Multiplexer #(.Bits(4)) multiplexer_1 (.sel(In[3]), .in_0(In), .in_1(undriven), .out(Output));
endmodule
