// Digital circuit 2-com.dig as structural Verilog
module _2_com (
  input  [3:0] _0,
  output [3:0] Out
);

  wire halfadder_2_c, halfadder_3_c, not_1_out, not_2_out, not_3_out;

  or or_1 (Out[3], Out[2], Out[1], Out[0]);
  not not_1 (not_1_out, _0[2]);
  HalfAdder halfadder_1 (.A(not_1_out), .B(halfadder_2_c), .S(Out[2]));  // open: C
  not not_2 (not_2_out, _0[1]);
  HalfAdder halfadder_2 (.A(not_2_out), .B(halfadder_3_c), .S(Out[1]), .C(halfadder_2_c));
  not not_3 (not_3_out, _0[0]);
  HalfAdder halfadder_3 (.A(not_3_out), .B(1'b1), .S(Out[0]), .C(halfadder_3_c));
endmodule
