// Digital circuit arithmetic functions.dig as structural Verilog
module arithmetic_functions (
  input  [3:0] A,
  input  [3:0] B,
  input  C,
  input  [2:0] Sel,
  output [3:0] OUT,
  output OWF
);

  wire _4_bitsadder_inator_1_p4, _4_bitsadder_inator_2_p4, _4_bitsadder_inator_3_p3,
       _4_bitsadder_inator_3_p4, _4_bitsadder_inator_4_p4, _4_bitsadder_inator_5_p4,
       _4_bitsadder_inator_6_p4, multiplexer_2_out, or_1_out, two_scompliment_inator_1_p2,
       two_scompliment_inator_2_p2;
  wire [3:0] _4_bitsadder_inator_1_p3, _4_bitsadder_inator_2_p3, _4_bitsadder_inator_4_p3,
       _4_bitsadder_inator_5_p3, _4_bitsadder_inator_6_p3, multiplexer_1_out;

  // TWO_sCompliment_inator two_scompliment_inator_1: pin names not known; wires that end beside it: B, two_scompliment_inator_1_p2
  // TWO_sCompliment_inator two_scompliment_inator_2: pin names not known; wires that end beside it: A, two_scompliment_inator_2_p2
  // _4_BitsAdder_inator _4_bitsadder_inator_1: pin names not known; wires that end beside it: A, 4'b1111, _4_bitsadder_inator_1_p3, _4_bitsadder_inator_1_p4
  // _4_BitsAdder_inator _4_bitsadder_inator_2: pin names not known; wires that end beside it: A, B, _4_bitsadder_inator_2_p3, _4_bitsadder_inator_2_p4
  // _4_BitsAdder_inator _4_bitsadder_inator_3: pin names not known; wires that end beside it: A, two_scompliment_inator_1_p2, _4_bitsadder_inator_3_p3, _4_bitsadder_inator_3_p4
  // _4_BitsAdder_inator _4_bitsadder_inator_4: pin names not known; wires that end beside it: two_scompliment_inator_2_p2, 4'b1111, _4_bitsadder_inator_4_p3, _4_bitsadder_inator_4_p4
  // _4_BitsAdder_inator _4_bitsadder_inator_5: pin names not known; wires that end beside it: _4_bitsadder_inator_3_p3, 4'b1111, _4_bitsadder_inator_5_p3, _4_bitsadder_inator_5_p4
  or or_1 (or_1_out, _4_bitsadder_inator_5_p4, _4_bitsadder_inator_3_p4);
  Multiplexer #(.Selector_Bits(3), .Bits(4)) multiplexer_1 (
    .sel(Sel), .in_0(A), .in_1(_4_bitsadder_inator_1_p3), .in_2(_4_bitsadder_inator_2_p3),
    .in_3(_4_bitsadder_inator_5_p3), .in_4(_4_bitsadder_inator_4_p3), .in_5(B), .in_6({A[2:0], 1'b0}),
    .in_7({1'b0, A[3:1]}), .out(multiplexer_1_out));
  // _4_BitsAdder_inator _4_bitsadder_inator_6: pin names not known; wires that end beside it: multiplexer_1_out, 4'b0001, _4_bitsadder_inator_6_p3, _4_bitsadder_inator_6_p4
  Multiplexer #(.Selector_Bits(3)) multiplexer_2 (
    .sel(Sel), .in_0(1'b0), .in_1(_4_bitsadder_inator_1_p4), .in_2(_4_bitsadder_inator_2_p4),
    .in_3(or_1_out), .in_4(_4_bitsadder_inator_4_p4), .in_5(1'b0), .in_6(1'b0), .in_7(1'b0),
    .out(multiplexer_2_out));
  Multiplexer #(.Bits(4)) multiplexer_3 (.sel(C), .in_0(multiplexer_1_out), .in_1(_4_bitsadder_inator_6_p3), .out(OUT));
  or or_2 (OWF, multiplexer_2_out, _4_bitsadder_inator_6_p4);
endmodule
