// Digital circuit Logical.dig as structural Verilog
module Logical (
  input  [3:0] Am0,
  input  [3:0] Bm0,
  input  [2:0] S,
  output [3:0] Out
);

  wire [3:0] and_1_out, and_2_out, nand_1_out, nor_1_out, not_1_out, or_1_out, xnor_1_out;

  assign nand_1_out = ~(Am0 & Bm0);  // NAnd nand_1, 4 bits wide
  assign nor_1_out = ~(Am0 | Bm0);  // NOr nor_1, 4 bits wide
  assign xnor_1_out = ~(Am0 ^ Bm0);  // XNOr xnor_1, 4 bits wide
  assign and_1_out = Am0 & Bm0;  // And and_1, 4 bits wide
  assign or_1_out = Am0 | Bm0;  // Or or_1, 4 bits wide
  assign and_2_out = Am0 & ~Bm0;  // And and_2, 4 bits wide
  assign not_1_out = ~Am0;  // Not not_1, 4 bits wide
  Multiplexer #(.Selector_Bits(3), .Bits(4)) multiplexer_1 (
    .sel(S), .in_0(not_1_out), .in_1(nand_1_out), .in_2(nor_1_out), .in_3(xnor_1_out), .in_4(and_1_out),
    .in_5(or_1_out), .in_6(and_2_out), .in_7(Am0), .out(Out));
endmodule
