// Digital circuit OldArithmetic.dig as structural Verilog
module OldArithmetic (
  input  [3:0] BM1,
  input  [3:0] AM1,
  input  [2:0] S,
  input  C,
  output [3:0] F,
  output Cout
);

  wire _4adder_1_cout, _4adder_6_cout, MC0_0, MC0_1, MC0_2, MC0_3, MC0_4, MC0_5;
  wire [3:0] _4adder_1_s, _4adder_2_s, _4adder_3_s, _4adder_4_s, _4adder_5_s, _4adder_6_s, _4adder_7_s,
       shiftleft_1_s, shiftr_1_s, two_scompliment_inator_1_p5, two_scompliment_inator_2_p2,
       two_scompliment_inator_3_p2, two_scompliment_inator_4_p2, two_scompliment_inator_5_p2;

  // TWO_sCompliment_inator two_scompliment_inator_1: pin names not known; wires that end beside it: 4'b0000, 4'b0001, C, 4'b0001, two_scompliment_inator_1_p5, BM1
  // TWO_sCompliment_inator two_scompliment_inator_2: pin names not known; wires that end beside it: BM1, two_scompliment_inator_2_p2
  // TWO_sCompliment_inator two_scompliment_inator_3: pin names not known; wires that end beside it: 4'b0001, two_scompliment_inator_3_p2
  _4Adder _4adder_1 (.A(AM1), .B(two_scompliment_inator_2_p2), .Cin(1'b0), .S(_4adder_1_s), .Cout(_4adder_1_cout));
  // TWO_sCompliment_inator two_scompliment_inator_4: pin names not known; wires that end beside it: AM1, two_scompliment_inator_4_p2
  _4Adder _4adder_2 (.A(AM1), .B(4'b0000), .Cin(C), .S(_4adder_2_s), .Cout(MC0_0));
  _4Adder _4adder_3 (.A(AM1), .B(two_scompliment_inator_3_p2), .Cin(C), .S(_4adder_3_s), .Cout(MC0_1));
  _4Adder _4adder_4 (.A(AM1), .B(BM1), .Cin(C), .S(_4adder_4_s), .Cout(MC0_2));
  // TWO_sCompliment_inator two_scompliment_inator_5: pin names not known; wires that end beside it: 4'b0001, two_scompliment_inator_5_p2
  _4Adder _4adder_5 (.A(4'b0000), .B(BM1), .Cin(C), .S(_4adder_5_s), .Cout(MC0_5));
  ShiftLeft shiftleft_1 (.In(AM1), .S(shiftleft_1_s));
  ShiftR shiftr_1 (.In(AM1), .S(shiftr_1_s));
  _4Adder _4adder_6 (.A(_4adder_1_s), .B(two_scompliment_inator_5_p2), .Cin(C), .S(_4adder_6_s), .Cout(_4adder_6_cout));
  _4Adder _4adder_7 (
    .A(two_scompliment_inator_4_p2), .B(two_scompliment_inator_1_p5), .Cin(C), .S(_4adder_7_s), .Cout(MC0_4));
  or or_1 (MC0_3, _4adder_6_cout, _4adder_1_cout);
  Multiplexer #(.Selector_Bits(3), .Bits(4)) multiplexer_1 (
    .sel(S), .in_0(_4adder_2_s), .in_1(_4adder_3_s), .in_2(_4adder_4_s), .in_3(_4adder_6_s),
    .in_4(_4adder_7_s), .in_5(_4adder_5_s), .in_6(shiftleft_1_s), .in_7(shiftr_1_s), .out(F));
  Multiplexer #(.Selector_Bits(3)) multiplexer_2 (
    .sel(S), .in_0(MC0_0), .in_1(MC0_1), .in_2(MC0_2), .in_3(MC0_3), .in_4(MC0_4), .in_5(MC0_5), .in_6(1'b0),
    .in_7(1'b0), .out(Cout));
endmodule
