// Digital circuit Template.dig as structural Verilog
module Template (
  input  [3:0] A,
  input  [3:0] B,
  input  [2:0] S,
  input  M,
  input  C,
  output [3:0] F,
  output COut
);

  wire [3:0] logical_1_out, oldarithmetic_1_f;

  Logical logical_1 (.Am0(A), .Bm0(B), .S(S), .Out(logical_1_out));
  OldArithmetic oldarithmetic_1 (.BM1(B), .AM1(A), .S(S), .C(C), .F(oldarithmetic_1_f), .Cout(COut));
  Multiplexer #(.Bits(4)) multiplexer_1 (.sel(M), .in_0(logical_1_out), .in_1(oldarithmetic_1_f), .out(F));
endmodule
