// Digital circuit 64-1.dig as structural Verilog
module _64_1 (
  input  [2:0] in_1,
  input  [2:0] in_2,
  output out_3
);

  wire comparator_1_eq, comparator_1_gt;
  wire [0:0] or_1_out;
  wire [2:0] add_1_s;

  Add #(.Bits(3)) add_1 (.a(in_1), .b(in_2), .c_i(1'b0), .s(add_1_s), .c_o(out_3));
  Comparator #(.Bits(3)) comparator_1 (
    .a(add_1_s), .b(3'b101), .gt(comparator_1_gt), .eq(comparator_1_eq));  // open: lt
  or or_1 (or_1_out[0], comparator_1_gt, comparator_1_eq);
  Seven_Seg_Hex seven_seg_hex_1 (.d({3'b000, or_1_out[0]}), .dp(1'b0));
endmodule
