// Digital circuit 64-2.dig as structural Verilog
module _64_2 (
  input  [2:0] in_1,
  output out_2,
  output out_3
);

  wire decoder_1_out_0, decoder_1_out_2, decoder_1_out_4, decoder_1_out_5, decoder_1_out_6, decoder_1_out_7;

  Decoder #(.Selector_Bits(3)) decoder_1 (
    .sel(in_1), .out_0(decoder_1_out_0), .out_2(decoder_1_out_2), .out_4(decoder_1_out_4),
    .out_5(decoder_1_out_5), .out_6(decoder_1_out_6), .out_7(decoder_1_out_7));  // open: out_1, out_3
  or or_1 (out_2, decoder_1_out_2, decoder_1_out_4, decoder_1_out_5, decoder_1_out_6);
  or or_2 (out_3, decoder_1_out_0, decoder_1_out_2, decoder_1_out_7, decoder_1_out_4, decoder_1_out_6);
endmodule
