// Digital circuit 66-2.dig as structural Verilog
module _66_2 (
  input  [2:0] in_1,
  input  [2:0] in_2,
  input  in_3,
  output [2:0] out_4
);

  wire [2:0] add_1_s, sub_1_s;

  Sub #(.Bits(3)) sub_1 (.a(in_1), .b(in_2), .c_i(1'b0), .s(sub_1_s));  // open: c_o
  Add #(.Bits(3)) add_1 (.a(in_1), .b(in_2), .c_i(1'b0), .s(add_1_s));  // open: c_o
  Multiplexer #(.Bits(3)) multiplexer_1 (.sel(in_3), .in_0(add_1_s), .in_1(sub_1_s), .out(out_4));
endmodule
