// Digital circuit 67-1.dig as structural Verilog
module _67_1 (
  input  A,
  input  B,
  input  C,
  input  D,
  input  E,
  input  A_2,
  input  B_2,
  input  C_2,
  output Y,
  output Y_2,
  output out_11
);

  wire and_1_out, and_2_out, and_3_out, and_4_out, and_5_out, and_6_out, and_7_out, and_8_out, and_9_out,
       and_10_out, and_11_out, and_12_out, and_13_out;

  and and_1 (and_1_out, A, D, E);
  and and_2 (and_2_out, A, C, E);
  and and_3 (and_3_out, A, B, E);
  and and_4 (and_4_out, A, C, D);
  and and_5 (and_5_out, A, B, D);
  and and_6 (and_6_out, A, B, C);
  and and_7 (and_7_out, B, D, E);
  and and_8 (and_8_out, B, C, E);
  and and_9 (and_9_out, B, C, D);
  and and_10 (and_10_out, C, D, E);
  or or_1 (Y, and_1_out, and_2_out, and_3_out, and_4_out, and_5_out, and_6_out, and_7_out, and_8_out, and_9_out, and_10_out);
  and and_11 (and_11_out, A_2, C_2);
  and and_12 (and_12_out, A_2, B_2);
  and and_13 (and_13_out, B_2, C_2);
  or or_2 (Y_2, and_11_out, and_12_out, and_13_out);
  xnor xnor_1 (out_11, Y_2, Y);
endmodule
