// Digital circuit 68-19.dig as structural Verilog
module _68_19 (
  input  [2:0] in_1,
  input  [2:0] in_2
);

  wire [0:0] comparator_1_eq;

  Comparator #(.Bits(3)) comparator_1 (.a(in_1), .b(in_2), .eq(comparator_1_eq[0]));  // open: gt, lt
  Seven_Seg_Hex seven_seg_hex_1 (.d({3'b000, comparator_1_eq[0]}), .dp(1'b0));
endmodule
