// Digital circuit 68-20.dig as structural Verilog
module _68_20 (
  input  [2:0] in_1,
  output out_2
);

  wire decoder_1_out_1, decoder_1_out_2, decoder_1_out_5, decoder_1_out_6;

  Decoder #(.Selector_Bits(3)) decoder_1 (
    .sel(in_1), .out_1(decoder_1_out_1), .out_2(decoder_1_out_2), .out_5(decoder_1_out_5),
    .out_6(decoder_1_out_6));  // open: out_0, out_3, out_4, out_7
  or or_1 (out_2, decoder_1_out_1, decoder_1_out_2, decoder_1_out_5, decoder_1_out_6);
endmodule
