// Digital circuit Template.dig as structural Verilog
module Template (
  input  J,
  input  K,
  input  Clock,
  input  Clear,
  output Q,
  output Q_2
);

  wire and_1_out, and_2_out, and_3_out, and_4_out, and_5_out, and_6_out, Clear_t, nor_1_out, nor_2_out,
       not_2_out, or_1_out, or_2_out;

  and and_1 (and_1_out, Q, K, Clock);
  and and_2 (and_2_out, Clock, J, Q_2);
  not not_1 (Clear_t, Clear);
  or or_1 (or_1_out, and_1_out, Clear);
  and and_3 (and_3_out, Clear_t, and_2_out);
  not not_2 (not_2_out, Clock);
  nor nor_1 (nor_1_out, or_1_out, nor_2_out);
  nor nor_2 (nor_2_out, nor_1_out, and_3_out);
  and and_4 (and_4_out, nor_2_out, not_2_out);
  and and_5 (and_5_out, not_2_out, nor_1_out);
  or or_2 (or_2_out, and_4_out, Clear);
  and and_6 (and_6_out, Clear_t, and_5_out);
  nor nor_3 (Q, or_2_out, Q_2);
  nor nor_4 (Q_2, Q, and_6_out);
endmodule
