// Digital circuit tem3.dig as structural Verilog
module tem3 (
  input  D,
  input  Clear,
  input  Clock,
  output Q,
  output Q_2
);

  wire nor_1_out;

  nor nor_1 (nor_1_out, Clear, ~D);  // NOr
  D_FF d_ff_1 (.D(nor_1_out), .C(Clock), .Q(Q), .nQ(Q_2));
endmodule
