// Digital circuit tem4.dig as structural Verilog
module tem4 (
  input  D,
  input  Clear,
  input  Clock,
  output Q,
  output Q_2
);

  wire nor_1_out, not_1_out;

  nor nor_1 (nor_1_out, Clear, not_1_out);
  not not_1 (not_1_out, D);
  D_FF d_ff_1 (.D(nor_1_out), .C(Clock), .Q(Q), .nQ(Q_2));
endmodule
