// Digital circuit tem2.dig as structural Verilog
module tem2 (
  input  T,
  input  Clear,
  input  Clock,
  output Q,
  output Q_2
);

  wire and_1_out, and_2_out, or_1_out;

  and and_1 (and_1_out, ~Clear, T);  // And
  or or_1 (or_1_out, and_2_out, and_1_out);
  T_FF t_ff_1 (.T(or_1_out), .C(Clock), .Q(Q), .nQ(Q_2));
  and and_2 (and_2_out, Q, Clear);
endmodule
