// Digital circuit 01Template.dig as structural Verilog
module _01Template (
  input  in_3,
  input  in_4,
  output Output,
  output Output_2
);

  wire and_1_out, and_2_out, not_1_out, not_2_out, not_3_out, not_4_out, or_1_out, or_2_out;

  not not_1 (not_1_out, in_4);
  not not_2 (not_2_out, in_3);
  and and_1 (and_1_out, in_3, not_1_out);
  and and_2 (and_2_out, not_2_out, in_4);
  not not_3 (not_3_out, in_3);
  not not_4 (not_4_out, in_4);
  or or_1 (or_1_out, in_3, in_4);
  or or_2 (or_2_out, not_3_out, not_4_out);
  or or_3 (Output, and_1_out, and_2_out);
  and and_3 (Output_2, or_1_out, or_2_out);

  // Other names for the same wires on the sheet: A = in_3; B = in_4
endmodule
