// Digital circuit 03Template.dig as structural Verilog
module _03Template (
  input  A,
  input  B,
  input  Cin,
  output Sum,
  output Cout,
  output Sum_2,
  output Cout_2
);

  wire and_1_out, and_2_out, and_3_out, and_4_out, and_5_out, and_6_out, and_7_out, not_1_out, not_2_out,
       not_3_out, not_4_out, not_5_out, not_6_out, or_3_out, or_4_out, or_5_out, or_6_out, or_7_out,
       or_8_out, or_9_out;

  not not_1 (not_1_out, A);
  not not_2 (not_2_out, B);
  not not_3 (not_3_out, Cin);
  and and_1 (and_1_out, not_1_out, not_2_out, Cin);
  and and_2 (and_2_out, not_1_out, B, not_3_out);
  and and_3 (and_3_out, A, not_2_out, not_3_out);
  and and_4 (and_4_out, A, B, Cin);
  and and_5 (and_5_out, A, B);
  and and_6 (and_6_out, B, Cin);
  and and_7 (and_7_out, A, Cin);
  or or_1 (Cout, and_5_out, and_6_out, and_7_out);
  or or_2 (Sum, and_1_out, and_2_out, and_3_out, and_4_out);
  not not_4 (not_4_out, A);
  not not_5 (not_5_out, B);
  not not_6 (not_6_out, Cin);
  or or_3 (or_3_out, A, B, Cin);
  or or_4 (or_4_out, A, not_5_out, not_6_out);
  or or_5 (or_5_out, not_4_out, B, not_6_out);
  or or_6 (or_6_out, not_4_out, not_5_out, Cin);
  or or_7 (or_7_out, A, B);
  or or_8 (or_8_out, A, Cin);
  or or_9 (or_9_out, B, Cin);
  and and_8 (Sum_2, or_3_out, or_4_out, or_5_out, or_6_out);
  and and_9 (Cout_2, or_7_out, or_8_out, or_9_out);
endmodule
