// Digital circuit 05Template.dig as structural Verilog
module _05Template (
  input  A,
  input  B,
  input  C,
  input  D,
  output Z1,
  output Z2,
  output Z3,
  output Z3_2,
  output Z2_2,
  output Z1_2
);

  wire and_1_out, and_2_out, and_3_out, and_4_out, and_5_out, and_6_out, and_7_out, and_8_out, and_9_out,
       and_10_out, and_12_out, and_13_out, and_14_out, and_15_out, not_1_out, not_2_out, not_3_out,
       not_4_out, not_5_out, not_6_out, not_7_out, not_8_out, or_4_out, or_5_out, or_6_out, or_7_out,
       or_8_out, or_9_out, or_10_out, or_11_out, or_12_out, or_13_out, or_14_out, or_15_out, or_16_out,
       or_17_out, or_18_out, or_19_out;

  not not_1 (not_1_out, A);
  not not_2 (not_2_out, B);
  not not_3 (not_3_out, C);
  not not_4 (not_4_out, D);
  and and_1 (and_1_out, A, not_3_out);
  and and_2 (and_2_out, B, not_3_out, not_4_out);
  and and_3 (and_3_out, A, B, not_4_out);
  and and_4 (and_4_out, not_1_out, C);
  and and_5 (and_5_out, not_1_out, not_2_out, D);
  and and_6 (and_6_out, not_2_out, C, D);
  and and_7 (and_7_out, not_1_out, not_2_out, not_3_out, not_4_out);
  and and_8 (and_8_out, not_1_out, B, not_3_out, D);
  and and_9 (and_9_out, A, B, C, D);
  and and_10 (and_10_out, A, not_2_out, C, not_4_out);
  or or_1 (Z1, and_1_out, and_2_out, and_3_out);
  or or_2 (Z2, and_4_out, and_5_out, and_6_out);
  or or_3 (Z3, and_7_out, and_8_out, and_9_out, and_10_out);
  not not_5 (not_5_out, A);
  not not_6 (not_6_out, B);
  not not_7 (not_7_out, C);
  not not_8 (not_8_out, D);
  or or_4 (or_4_out, A, not_7_out);
  or or_5 (or_5_out, A, not_8_out);
  or or_6 (or_6_out, A, B, C);
  or or_7 (or_7_out, not_5_out, not_7_out, not_8_out);
  or or_8 (or_8_out, not_5_out, B, not_7_out);
  or or_9 (or_9_out, C, D);
  or or_10 (or_10_out, not_5_out, not_6_out);
  or or_11 (or_11_out, not_6_out, not_7_out);
  or or_12 (or_12_out, not_5_out, C);
  or or_13 (or_13_out, not_5_out, not_7_out, D);
  or or_14 (or_14_out, A, B, not_8_out);
  or or_15 (or_15_out, not_6_out, not_7_out, D);
  or or_16 (or_16_out, not_5_out, B, not_8_out);
  or or_17 (or_17_out, not_6_out, C, D);
  or or_18 (or_18_out, not_5_out, C);
  or or_19 (or_19_out, A, not_7_out);
  and and_11 (Z1_2, or_4_out, or_5_out, or_6_out, or_7_out, or_8_out);
  and and_12 (and_12_out, or_9_out, or_10_out, or_11_out);
  and and_13 (and_13_out, or_12_out, or_13_out);
  and and_14 (and_14_out, or_14_out, or_15_out, or_16_out);
  and and_15 (and_15_out, or_17_out, or_18_out, or_19_out);
  and and_16 (Z2_2, and_12_out, and_13_out);
  and and_17 (Z3_2, and_14_out, and_15_out);
endmodule
